// Logisim project basic.circ as structural Verilog: 1 circuit, main circuit main
module main (
  input  a,
  input  b,
  output y
);

  wire and_1_out;

  and and_1 (and_1_out, a, b);
  not not_1 (y, and_1_out);
endmodule
